# Fritzing sketch 386-2 (saved by Fritzing 0.3.19b)
breadboards: 1

parts:
  IC2 = IC, DIP package, 8 pins [chip_label=LM386 spacing=300mil]
  C2 = Ceramic Capacitor [package=THT]
  C3 = Electrolytic Capacitor [package=THT]

nets:
  N1: IC2.pin2, C2.pin_0
  N2: IC2.pin3, IC2.pin4
  N3: IC2.pin5, C3.+
