# Fritzing sketch 386 (saved by Fritzing 0.3.19b)
breadboards: 1

parts:
  IC2 = IC, DIP package, 8 pins [chip_label=LM386 spacing=300mil]
  C1 = Electrolytic Capacitor [package=THT]
  C2 = Ceramic Capacitor [package=THT]
  R1 = Resistor [resistance=10 package=THT]
  R2 = Rotary Potentiometer (Small)
  C3 = Electrolytic Capacitor [package=THT]
  SPKR1 = Loudspeaker
  C4 = Ceramic Capacitor [package=THT]

nets:
  N1: IC2.pin1, R2.leg1
  N2: IC2.pin2, C2.pin_0
  N3: IC2.pin3, IC2.pin4, C1.-, C4.pin_1
  N4: IC2.pin5, R1.Pin_0, C3.+
  N5: IC2.pin6, C1.+
  N6: IC2.pin8, R2.wiper
  N7: R1.Pin_1, C4.pin_0
  N8: C3.-, SPKR1.pin2
