# Fritzing sketch 4093-quad (saved by Fritzing 0.3.10b)
breadboards: 1

parts:
  IC2 = IC, DIP package, 14 pins [chip_label=4093]
  C1 = Ceramic Capacitor [package=THT]
  C1_2 = Ceramic Capacitor [package=THT]

nets:
  N1: IC2.pin1, IC2.pin14
  N2: IC2.pin2, C1.pin_0
  N3: IC2.pin3, IC2.pin6
  N4: IC2.pin4, IC2.pin8
  N5: IC2.pin5, C1_2.pin_1
  N6: IC2.pin7, C1.pin_1, C1_2.pin_0
