# Fritzing sketch 4093-single (saved by Fritzing 0.3.10b)
breadboards: 1

parts:
  IC2 = IC, DIP package, 14 pins [chip_label=4093]
  C1 = Ceramic Capacitor [package=THT]

nets:
  N1: IC2.pin1, IC2.pin14
  N2: IC2.pin2, C1.pin_0
  N3: IC2.pin7, C1.pin_1
