# Fritzing sketch 5206 (saved by Fritzing 0.3.10b)
breadboards: 1

parts:
  IC1 = IC, DIP package, 24 pins [chip_label=AD5206 spacing=300mil]
  DC_Power1 = DC Power [voltage=5]

nets:
  GND: IC1.pin1, IC1.pin4, IC1.pin9, IC1.pin12, IC1.pin15, IC1.pin18, IC1.pin19, IC1.pin22, DC_Power1.GND
  N1: IC1.pin6, DC_Power1.V+
